# Fritzing sketch pca9544a_bmp180 (saved by Fritzing 0.9.2b)
circuit board: 8.46667cm x 5.64444cm
breadboards: 1

parts:
  BMP1 = BMP085 Breakout
  BMP2 = BMP085 Breakout
  R6 = Resistor [tolerance=±5% resistance=4.7k package=THT]
  R7 = Resistor [tolerance=±5% resistance=4.7k package=THT]
  R8 = Resistor [tolerance=±5% resistance=4.7k package=THT]
  IC1 = IC, DIP package, 20 pins [chip_label=PCA9544A]
  R10 = Resistor [tolerance=±5% resistance=4.7k package=THT]
  R11 = Resistor [tolerance=±5% resistance=4.7k package=THT]
  R13 = Resistor [tolerance=±5% resistance=10k package=THT]
  R14 = Resistor [tolerance=±5% resistance=10k package=THT]
  R15 = Resistor [tolerance=±5% resistance=4.7k package=THT]
  R17 = Resistor [tolerance=±5% resistance=10k package=THT]
  R19 = Resistor [tolerance=±5% resistance=10k package=THT]
  R20 = Resistor [tolerance=±5% resistance=10k package=THT]
  R21 = Resistor [tolerance=±5% resistance=10k package=THT]

nets:
  N1: BMP1.SCL, IC1.pin16, R15.Pin_0
  N2: BMP1.SDA, R7.Pin_0, IC1.pin15
  GND: BMP1.GND, BMP2.GND, R6.Pin_0, R7.Pin_1, R8.Pin_0, IC1.pin20, R15.Pin_1, R17.Pin_1, R19.Pin_1, R20.Pin_1
  N3: BMP2.VIN, IC1.pin10, R10.Pin_0, R11.Pin_0, R13.Pin_0, R14.Pin_0, R21.Pin_1
  N4: BMP2.SCL, R8.Pin_1, IC1.pin9
  N5: BMP2.SDA, R6.Pin_1, IC1.pin8
  N6: IC1.pin1, IC1.pin2, R21.Pin_0
  N7: IC1.pin3, R17.Pin_0
  N8: IC1.pin4, R19.Pin_0
  N9: IC1.pin7, R20.Pin_0
  N10: IC1.pin11, R13.Pin_1
  N11: IC1.pin14, R14.Pin_1
  N12: IC1.pin18, R11.Pin_1
  N13: IC1.pin19, R10.Pin_1

notes:
  GND
  SCL
  SDA
  +V
  4.7k resistors are optional. Verify your I2C bus already has pull-up resistors to omit
  10k resistors are required
  PCA9544A is surface mount only. You will need a breakout board

custom parts:
  BMP085 Breakout: A breakout for the BMP085 barometric pressure and temperature sensor
